# Fritzing sketch Diagram (saved by Fritzing 0.9.4)

parts:
  VCC1 = 4 x AAA Battery Mount
  S1 = Pushbutton [package="[SMD]"]
  Part1 = 12 NeoPixel Ring [part_number=1643]
  M2 = RioRand LM2596
  U1 = ESP32-38PinWide [part_number=ESP32-38PinWide]
  S2 = Tilt Switch [package=THT]

nets:
  N1: VCC1.-, M2.Pin_2
  N2: VCC1.+, M2.Pin_1
  GND: S1.Pin_1, S1.Pin_2, Part1.GND, M2.Pin_4, U1.GND, S2.Pin_1
  N3: S1.Pin_3, S1.Pin_4, U1.GPIO33
  N4: Part1.IN, U1.GPIO17
  VDD: Part1.VDD, M2.Pin_3, U1.VIN
  N5: U1.GPIO34, S2.Pin_2

custom parts:
  12 NeoPixel Ring: 12 ultra bright smart LED NeoPixels are arranged in a circle with 1.5" (37mm) outer diameter. The rings are 'chainable' - connect the output pin of one to the input pin of another. Use only one microcontroller pin to control as many as you can chain together! Each LED is addressable as the driver chip is inside the LED. Each one has ~18mA constant current drive so the color will be very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
  ESP32-38PinWide: Generic 38-Pin ESP32 with wide format (only access to one side of pins on a breadboard) based on Stephen Lilley's HiLetgo ESP-WROOM-32 ESP32 ESP-32S Development Board.
